# Fritzing sketch minipong (saved by Fritzing 0.8.5b)
circuit board: 8.46667cm x 5.64444cm
breadboards: 2

parts:
  Part1 = Arduino Uno (Rev3)
  R1 = Rotary Potentiometer (Small) [maximum_resistance=100kΩ package=THT]
  R2 = Rotary Potentiometer (Small) [maximum_resistance=100kΩ package=THT]  # not connected
  R3 = Rotary Potentiometer (Small) [maximum_resistance=100kΩ package=THT]
  LCD1 = LCD screen
  R4 = Resistor [tolerance=±5% resistance=220 package=THT]
  S1 = Pushbutton [package="[THT]"]
  R5 = Resistor [tolerance=±5% resistance=10k package=THT]

nets (from the breadboard view):
  N1: Part1.A1, R1.wiper
  N2: Part1.D11_PWM/MOSI, LCD1.E
  N3: Part1.D12/MISO, LCD1.RS
  N4: Part1.D2, LCD1.DB7
  N5: Part1.D3_PWM, LCD1.DB6
  N6: Part1.D4, LCD1.DB5
  N7: Part1.D5_PWM, LCD1.DB4
  N8: Part1.D7, S1.Pin_3, S1.Pin_4, R5.Pin_1
  5V: Part1.5V, R1.leg1, R3.leg2, LCD1.VDD, R4.Pin_0, S1.Pin_1, S1.Pin_2
  GND: Part1.GND, R1.leg2, R3.leg1, LCD1.VSS, LCD1.R/W, LCD1.LED-, R5.Pin_0
  N9: R3.wiper, LCD1.V0
  N10: LCD1.LED+, R4.Pin_1
